// Logisim project test.circ as structural Verilog: 1 circuit, main circuit main
module main (
  input  in_1,
  input  in_2,
  input  in_3,
  input  in_4,
  output out_5,
  output out_6,
  output out_7
);

  wire and_1_out, and_2_out, and_3_out, or_1_out, undriven, undriven_2, undriven_3, undriven_4, undriven_5,
       undriven_6, undriven_7, undriven_8, undriven_9, undriven_10, undriven_11, undriven_12, undriven_13,
       undriven_14, xor_1_out, xor_2_out, xor_3_out;

  xor xor_1 (xor_1_out, undriven, undriven_2);
  and and_1 (and_1_out, undriven_3, undriven_4);
  xor xor_2 (xor_2_out, undriven_5, undriven_6);
  and and_2 (and_2_out, undriven_7, undriven_8);
  xor xor_3 (xor_3_out, undriven_9, undriven_10);
  and and_3 (and_3_out, undriven_11, undriven_12);
  or or_1 (or_1_out, undriven_13, undriven_14);
endmodule
