// Logisim project gate.circ as structural Verilog: 1 circuit, main circuit main
module main (
);

  // NOT_Gate not_1 is placed but not wired
  // AND_Gate and_1 is placed but not wired
  // OR_Gate or_1 is placed but not wired
  // XOR_Gate xor_1 is placed but not wired
  // NAND_Gate nand_1 is placed but not wired
endmodule
